# Fritzing sketch sketch (saved by Fritzing 0.9.2b)

parts:
  Part1 = Arduino Nano (Rev3.0) (ICSP)
  Part2 = DeuLigne 1.1 - The Snootlab's LCD shield for Arduino
  ADXL1 = ADXL335 Accelerometer Breakout
  microSD1 = MicroSD Breakout
  J1 = Piezo Speaker
  VCC1 = Battery

nets:
  GND: Part1.GND, Part2.GND, ADXL1.GND, microSD1.GND, J1.pin1, VCC1.-
  N1: Part1.D3, J1.pin2
  N2: Part1.D10, microSD1.CS
  N3: Part1.D11/MOSI, microSD1.DI
  N4: Part1.D12/MISO, microSD1.DO
  N5: Part1.VIN, VCC1.+
  5V: Part1.5V, Part2.+5V, ADXL1.Vin, microSD1.5V
  N6: Part1.A5, Part2.A5(CLK), ADXL1.Yout
  N7: Part1.A4, Part2.A4(SDA), ADXL1.Zout
  N8: Part1.D13/SCK, microSD1.CLK

custom parts:
  ADXL335 Accelerometer Breakout: ADXL335 Accelerometer Breakout board
  MicroSD Breakout: 5V-ready microSD Breakout with Level Shifter
